# Fritzing sketch RobotGirlOnNewYearsEveBall-1987 (saved by Fritzing 0.9.2b)
perfboards: 1

parts:
  Q2 = NPN-Transistor [package="TO92 [THT]"]
  Q3 = NPN-Transistor [package="TO92 [THT]"]
  Q4 = NPN-Transistor [package="TO92 [THT]"]
  R1 = Trimmer Potentiometer [maximum_resistance=10kΩ package=THT]  # not connected
  LED3 = smd LED [color="Red (633nm)" package="0603 [SMD]"]
  LED4 = smd LED [color="Red (633nm)" package="0603 [SMD]"]
  Q1 = NPN-Transistor [package="TO92 [THT]"]
  R2 = Resistor [tolerance=±5% resistance=22 package=THT]
  LED2 = LED - 5mm [color="Red (633nm)" package="5 mm [THT]"]
  R3 = Resistor [tolerance=±5% resistance=22 package=THT]
  R4 = Resistor [tolerance=±5% resistance=22 package=THT]
  R5 = Resistor [tolerance=±5% resistance=22 package=THT]
  V1 = DC Power [voltage=5]
  LED1 = smd LED [color="Red (633nm)" package="0603 [SMD]"]
  Part1 = Arduino Pro Mini v13  # not connected
  SW1 = DIP Switch 8 Position [package=dipswitch-08]  # not connected
  R6 = TRIMPOT [package=trimpot_tc33]  # not connected
  J1 = Power Jack [package=power_jack_pth]  # not connected

nets:
  GND: Q2.E, Q3.E, Q4.E, Q1.E, V1.V-
  N1: Q2.C, R4.Pin_0
  N2: Q3.C, R3.Pin_0
  N3: Q4.C, R2.Pin_0
  N4: LED3.anode, R3.Pin_1
  N5: LED4.cathode, V1.V+, LED1.cathode
  N6: LED4.anode, R2.Pin_1
  N7: Q1.C, R5.Pin_0
  N8: LED2.anode, R4.Pin_1
  N9: R5.Pin_1, LED1.anode
